// Logisim project cpu.circ as structural Verilog: 3 circuits, main circuit main
module main (
  input  [31:0] INSTRUCTION,
  input  CLOCK,
  output [31:0] FETCH_ADDRESS,
  output [31:0] s0_Value,
  output [31:0] s1_Value,
  output [31:0] s2_Value,
  output [31:0] ra_Value,
  output [31:0] HI_Value,
  output [31:0] LO_Value
);

  wire main_2_signed_overflow, MEM_p1, MEM_p5, MEM_p7, MEM_p10, MEM_p13, MEM_p16, undriven_2;
  wire [4:0] writeregister;
  wire [5:0] undriven;
  wire [31:0] adder_1_out, adder_2_out, extend, main_1_read_data_1, main_1_read_data_2, main_2_result,
       MEM_p8, multiplexer_2_out, multiplexer_3_out, PC_q, shifter_1_out, writedata;

  maincontrol maincontrol_1 (.instruction(undriven));  // open: RegDst, Jump, Branch, MemRead, MemToReg, ALUOP, MemWrite, ALUSrc, RegWrite
  assign extend = {{16{1'b0}}, INSTRUCTION[15:0]};  // Bit_Extender bit_extender_1
  regfile_main main_1 (
    .Read_Register_1(INSTRUCTION[25:21]), .Read_Register_2(INSTRUCTION[20:16]),
    .Write_Register(writeregister), .Write_Data(writedata), .Clock(CLOCK), .Read_Data_1(main_1_read_data_1),
    .Read_Data_2(main_1_read_data_2), .s0_Value(s0_Value), .s1_Value(s1_Value), .s2_Value(s2_Value),
    .ra_Value(ra_Value));  // open: Write_Enable, in_5
  Multiplexer #(.width(5)) multiplexer_1 (
    .in0(INSTRUCTION[20:16]), .in1(INSTRUCTION[15:11]), .out(writeregister));  // open: sel, en
  LED led_1 (.in(main_2_signed_overflow));
  Multiplexer #(.width(32)) multiplexer_2 (
    .in0(main_1_read_data_2), .in1(extend), .out(multiplexer_2_out));  // open: sel, en
  alu_main main_2 (
    .X(main_1_read_data_1), .Result(main_2_result), .Signed_Overflow(main_2_signed_overflow),
    .Y(multiplexer_2_out));  // open: Switch, Equal, Result_2
  Register #(.width(32)) LO ();  // open: D, en, Q, clk, clr
  Multiplexer #(.width(32)) multiplexer_3 (
    .in0(adder_1_out), .in1(adder_2_out), .out(multiplexer_3_out), .sel(undriven_2));  // open: en
  Register #(.width(32)) HI ();  // open: D, en, Q, clk, clr
  Register #(.width(32)) PC (.D(multiplexer_3_out), .Q(PC_q), .clk(CLOCK));  // open: en, clr
  // mem_main MEM: pin names not known; wires that end beside it: MEM_p1, MEM_p1, main_2_result, main_1_read_data_2, MEM_p5, MEM_p5, MEM_p7, MEM_p8, MEM_p7, MEM_p10, MEM_p10, HI_Value, MEM_p13, MEM_p13, LO_Value, MEM_p16
  Multiplexer #(.width(32)) multiplexer_4 (.in0(main_2_result), .in1(MEM_p8), .out(writedata));  // open: sel, en
  Multiplexer #(.width(32)) multiplexer_5 (.in0(PC_q), .in1({32{1'b0}}), .out(FETCH_ADDRESS));  // open: sel, en
  Adder #(.width(32)) adder_1 (.a(PC_q), .b(32'h4), .out(adder_1_out));  // open: cin, cout
  Shifter #(.width(32)) shifter_1 (.in(extend), .\dist (5'b00010), .out(shifter_1_out));
  Adder #(.width(32)) adder_2 (.a(adder_1_out), .b(shifter_1_out), .out(adder_2_out));  // open: cin, cout

  // Other names for the same wires on the sheet: clk = CLOCK; fetch_addr[31:0] = FETCH_ADDRESS;
  //   readregister2[4:0] = INSTRUCTION[20:16]; readregister1[4:0] = INSTRUCTION[25:21]; jump[31:0] = extend;
  //   ra[31:0] = ra_Value; s0[31:0] = s0_Value; s1[31:0] = s1_Value; s2[31:0] = s2_Value

  // Notes on the sheet:
  //   Output
  //   These are outputs/inputs from run.circ
  //   Inputs
  //   These are DEBUG/TEST outputs from your circuit.
endmodule

module maincontrol (
  input  [5:0] instruction,
  output RegDst,
  output Jump,
  output Branch,
  output MemRead,
  output MemToReg,
  output [1:0] ALUOP,
  output MemWrite,
  output ALUSrc,
  output RegWrite
);

  wire [9:0] multiplexer_1_out, multiplexer_2_out;

  Multiplexer #(.select(5), .width(10)) multiplexer_1 (
    .in0(10'h241), .in2(10'h2), .in3(10'h2), .in5(10'h44), .in8(10'h300), .in9(10'h300), .in10(10'h3b8),
    .in11(10'h180), .in12(10'h380), .in13(10'h340), .in15(10'h318), .out(multiplexer_1_out),
    .sel(instruction[4:0]));  // open: in1, in4, in6, in7, in14, in16, in17, in18, in19, in20, in21, in22, in23, in24, in25, in26, in27, in28, in29, in30, in31, en
  Multiplexer #(.select(5), .width(10)) multiplexer_2 (
    .in0(10'h318), .in3(10'h318), .in5(10'h300), .in8(10'h180), .in9(10'h180), .in10(10'h3b8),
    .in11(10'h180), .in12(10'h80), .in13(10'h340), .in15(10'h318), .out(multiplexer_2_out),
    .sel(instruction[4:0]));  // open: in1, in2, in4, in6, in7, in14, in16, in17, in18, in19, in20, in21, in22, in23, in24, in25, in26, in27, in28, in29, in30, in31, en
  Multiplexer #(.width(10)) multiplexer_3 (
    .in0(multiplexer_1_out), .in1(multiplexer_2_out),
    .out({RegWrite, ALUSrc, MemWrite, ALUOP, MemToReg, MemRead, Branch, Jump, RegDst}), .sel(instruction[5]));  // open: en

  // Other names for the same wires on the sheet: mux1[4:0] = instruction[4:0]
endmodule

module alucontrol (
  input  [5:0] function_code,
  input  [1:0] alu_op,
  output [3:0] ALUSwitch
);

  wire [3:0] function_out, multiplexer_1_out, multiplexer_2_out, undriven;

  Multiplexer #(.select(5), .width(4)) multiplexer_1 (
    .in0(undriven), .in1(undriven), .in2(undriven), .in3(undriven), .in4(undriven), .in5(undriven),
    .in6(undriven), .in7(undriven), .in8(undriven), .in9(undriven), .in10(undriven), .in11(undriven),
    .in12(undriven), .in13(undriven), .in14(undriven), .in15(undriven), .in16(undriven), .in17(undriven),
    .in18(undriven), .in19(undriven), .in20(undriven), .in21(undriven), .in22(undriven), .in23(undriven),
    .in24(undriven), .in25(undriven), .in26(undriven), .in27(undriven), .in28(undriven), .in29(undriven),
    .in30(undriven), .in31(undriven), .out(multiplexer_1_out), .sel(function_code[4:0]));  // open: en
  Multiplexer #(.select(5), .width(4)) multiplexer_2 (
    .in0(4'b0101), .in1(4'b0110), .in3(4'b1010), .out(multiplexer_2_out), .sel(function_code[4:0]));  // open: in2, in4, in5, in6, in7, in8, in9, in10, in11, in12, in13, in14, in15, in16, in17, in18, in19, in20, in21, in22, in23, in24, in25, in26, in27, in28, in29, in30, in31, en
  Multiplexer #(.width(4)) multiplexer_3 (
    .in0(multiplexer_1_out), .in1(multiplexer_2_out), .out(function_out), .sel(function_code[5]));  // open: en
  Multiplexer #(.select(2), .width(4)) multiplexer_4 (
    .in0(4'b0101), .in1(4'b0111), .in2(function_out), .out(ALUSwitch), .sel(alu_op));  // open: in3, en

  // Other names for the same wires on the sheet: function[5:0] = function_code; mux1[4:0] = function_code[4:0];
  //   mux2 = function_code[5]
endmodule
